# Fritzing sketch Testador de Componentes (saved by Fritzing 0.8.0b)
breadboards: 2

parts:
  LCD1 = LCD screen
  R2 = Resistor [tolerance=±5% resistance=220 package=THT]
  J1 = female pin header, 3 pins [form="♀ (female)"]
  R3 = Resistor [tolerance=±5% resistance=680 package=THT]
  R4 = Resistor [tolerance=±5% resistance=470 package=THT]
  R5 = Resistor [tolerance=±5% resistance=680 package=THT]
  R6 = Resistor [tolerance=±5% resistance=470 package=THT]
  R7 = Resistor [tolerance=±5% resistance=470 package=THT]
  R8 = Resistor [tolerance=±5% resistance=680 package=THT]
  Contrast1 = Rotary Potentiometer (Small) [maximum_resistance=100kΩ]
  Arduino1 = Arduino Uno (Rev3)

nets:
  VSS: LCD1.VSS, LCD1.R/W, LCD1.LED-, Contrast1.leg1, Arduino1.GND
  VDD: LCD1.VDD, R2.Pin_1, Contrast1.leg2, Arduino1.5V
  N1: LCD1.V0, Contrast1.wiper
  N2: LCD1.RS, Arduino1.D12/MISO
  N3: LCD1.E, Arduino1.D11_PWM/MOSI
  N4: LCD1.DB4, Arduino1.D5_PWM
  N5: LCD1.DB5, Arduino1.D4
  N6: LCD1.DB6, Arduino1.D3_PWM
  N7: LCD1.DB7, Arduino1.D2
  N8: LCD1.LED+, R2.Pin_0
  N9: J1.pin1, R7.Pin_0, R8.Pin_0, Arduino1.A2
  N10: J1.pin2, R5.Pin_0, R6.Pin_0, Arduino1.A1
  N11: J1.pin3, R3.Pin_0, R4.Pin_0, Arduino1.A0
  N12: R3.Pin_1, Arduino1.D10_PWM/SS
  N13: R4.Pin_1, Arduino1.ICSP_SCK, Arduino1.D13/SCK
  N14: R5.Pin_1, Arduino1.D8
  N15: R6.Pin_1, Arduino1.D9_PWM
  N16: R7.Pin_1, Arduino1.D7
  N17: R8.Pin_1, Arduino1.D6_PWM

notes:
  Code and more on character LCDs at http://arduino.cc/en/Tutorial/LiquidCrystal
